# Fritzing sketch epir (saved by Fritzing 0.7.0b)
breadboards: 1

parts:
  Arduino1 = Arduino
  R1 = Resistor [tolerance=±5% resistance=10k package=THT]
  zilog_ePir = mystery part, 8 pins [chip_label="ZILOG ePIR" spacing=300mil]
  LED1 = LED - 5mm [color="Red (633nm)" package="5 mm [THT]"]
  R2 = Resistor [tolerance=±5% resistance=220 package=THT]

nets:
  N1: Arduino1.GND, zilog_ePir.pin1, zilog_ePir.pin3, zilog_ePir.pin4, LED1.anode
  N2: Arduino1.D9, R2.Pin_1
  N3: Arduino1.D2, zilog_ePir.pin5
  N4: Arduino1.3V3, R1.Pin_0, zilog_ePir.pin2
  N5: R1.Pin_1, zilog_ePir.pin6
  N6: LED1.cathode, R2.Pin_0
